// Logisim project cpu.circ as structural Verilog: 1 circuit, main circuit main
module main (
  input  in_1
);

  wire and_1_out, and_2_out, and_3_out, and_4_out, and_5_out, and_6_out, CLK, d_ff_1_q, d_ff_2_q,
       decoder_1_out0, decoder_1_out1, decoder_1_out4, decoder_2_out0, decoder_2_out1, decoder_2_out3,
       decoder_2_out4, decoder_2_out5, decoder_3_out0, decoder_3_out1, decoder_3_out2, decoder_3_out3,
       decoder_3_out4, decoder_3_out5, decoder_3_out6, decoder_3_out7, decoder_4_out0, decoder_4_out1,
       decoder_4_out2, decoder_4_out3, decoder_4_out4, decoder_4_out5, END_INST_out, MEM_CLK, MEM_O_EN,
       nor_1_out, nor_2_out, not_1_out, not_2_out, not_3_out, not_4_out, or_1_out, or_2_out, or_3_out,
       or_4_out, or_5_out, or_6_out, or_7_out, or_8_out, or_9_out, or_10_out, or_11_out, or_12_out,
       or_13_out, or_15_out, xor_1_out, xor_2_out, xor_3_out;
  wire [3:0] counter_1_q, rom_1_data, rom_1_data_2;
  wire [7:0] ACC_H_q, ACC_L_q, comparator_1_eq, controlled_buffer_7_out, controlled_buffer_11_out, DATA,
       DATA_LATCH_H_q, DATA_LATCH_L_q, demultiplexer_1_out0, demultiplexer_1_out1, multiplexer_6_out,
       multiplexer_9_out, OPCODE_LATCH_q, rom_1_data_3;
  wire [15:0] adder_1_out, adder_2_out, adder_3_out, ADDRESS, ALU_IN_LATCH_q, controlled_buffer_1_out,
       controlled_buffer_4_out, controlled_buffer_10_out, IP_q, multiplexer_1_out, multiplexer_2_out,
       multiplexer_3_out, multiplexer_4_out, multiplexer_5_out, multiplexer_7_out, shift_register_1_p5,
       subtractor_1_out;
  wire [15:1] multiplexer_8_out;

  xor xor_1 (xor_1_out, CLK, d_ff_1_q);
  D_Flip_Flop d_ff_1 (.D(and_1_out), .clk(or_5_out), .Q(d_ff_1_q));  // open: Qn, preset, reset
  and and_1 (and_1_out, CLK, d_ff_2_q);
  D_Flip_Flop d_ff_2 (.D(1'b1), .clk(CLK), .Q(d_ff_2_q), .reset(or_2_out));  // open: Qn, preset
  Register #(.width(16)) ALU_IN_LATCH (
    .D(controlled_buffer_4_out), .en(decoder_3_out7), .clk(multiplexer_5_out[0]), .Q(ALU_IN_LATCH_q));  // open: clr
  Decoder #(.select(4)) decoder_1 (
    .out0(decoder_1_out0), .out1(decoder_1_out1), .out4(decoder_1_out4), .sel(rom_1_data_2),
    .en(decoder_2_out5));  // open: out2, out3, out5, out6, out7, out8, out9, out10, out11, out12, out13, out14, out15
  not not_1 (not_1_out, xor_1_out);
  nor nor_1 (nor_1_out, OPCODE_LATCH_q[0], OPCODE_LATCH_q[1], OPCODE_LATCH_q[2], OPCODE_LATCH_q[3], OPCODE_LATCH_q[4], OPCODE_LATCH_q[5], OPCODE_LATCH_q[6], OPCODE_LATCH_q[7]);
  or or_1 (or_1_out, or_2_out, or_5_out);
  // Shift_Register shift_register_1: pin names not known; wires that end beside it: or_1_out, 1'b1, xor_1_out, 1'b1, shift_register_1_p5[0], shift_register_1_p5[2]
  // Shift_Register shift_register_2: pin names not known; wires that end beside it: or_1_out, 1'b1, not_1_out, 1'b1, shift_register_1_p5[4], shift_register_1_p5[6], shift_register_1_p5[8], shift_register_1_p5[10], shift_register_1_p5[12], shift_register_1_p5[14], shift_register_1_p5[1], shift_register_1_p5[3], shift_register_1_p5[5], shift_register_1_p5[7], shift_register_1_p5[9], shift_register_1_p5[11], shift_register_1_p5[13], shift_register_1_p5[15]
  and and_2 (and_2_out, decoder_3_out6, multiplexer_5_out[0]);
  Multiplexer #(.width(16)) multiplexer_1 (
    .in0({16{1'b0}}), .in1(shift_register_1_p5), .out(multiplexer_1_out), .sel(decoder_2_out0));
  assign controlled_buffer_1_out = decoder_1_out0 ? adder_1_out : 16'bz;  // Controlled_Buffer controlled_buffer_1
  Adder #(.width(16)) adder_1 (.a(ALU_IN_LATCH_q), .b(controlled_buffer_4_out), .out(adder_1_out));  // open: cin, cout
  Subtractor #(.width(16)) subtractor_1 (
    .a(ALU_IN_LATCH_q), .b(controlled_buffer_4_out), .out(subtractor_1_out));  // open: bin, bout
  assign controlled_buffer_1_out = decoder_1_out4 ? ALU_IN_LATCH_q : 16'bz;  // Controlled_Buffer controlled_buffer_2
  Register OPCODE_LATCH (
    .D(controlled_buffer_4_out[7:0]), .en(decoder_3_out6), .clk(multiplexer_5_out[0]), .Q(OPCODE_LATCH_q),
    .clr(END_INST_out));
  or END_INST (END_INST_out, in_1, nor_2_out);
  or or_2 (or_2_out, and_2_out, END_INST_out);
  assign controlled_buffer_1_out = decoder_1_out1 ? subtractor_1_out : 16'bz;  // Controlled_Buffer controlled_buffer_3
  Multiplexer #(.width(16)) multiplexer_2 (
    .in0({16{1'b0}}), .in1(controlled_buffer_4_out), .out(multiplexer_2_out), .sel(decoder_1_out4));
  nor nor_2 (nor_2_out, rom_1_data_3[0], rom_1_data_3[1], rom_1_data_3[2], rom_1_data_3[3], rom_1_data_3[4], rom_1_data_3[5], rom_1_data_3[6], rom_1_data_3[7], rom_1_data[0], rom_1_data[1], rom_1_data[2], rom_1_data[3], rom_1_data_2[0], rom_1_data_2[1], rom_1_data_2[2], rom_1_data_2[3]);
  Register #(.width(16)) IP (.D(multiplexer_3_out), .en(or_3_out), .clk(or_4_out), .Q(IP_q), .clr(in_1));
  Multiplexer #(.width(16)) multiplexer_3 (
    .in0(controlled_buffer_4_out), .in1(adder_2_out), .out(multiplexer_3_out), .sel(decoder_2_out0));
  or or_3 (or_3_out, decoder_2_out0, decoder_3_out4);
  or or_4 (or_4_out, multiplexer_1_out[0], multiplexer_5_out[0]);
  Counter #(.max('hf), .width(4)) counter_1 (
    .clr(or_2_out), .up(1'b1), .clk(or_5_out), .Q(counter_1_q));  // open: load, count, D, carry
  assign controlled_buffer_4_out = decoder_4_out4 ? IP_q : 16'bz;  // Controlled_Buffer controlled_buffer_4
  Comparator #(.width(16)) comparator_1 (
    .a(controlled_buffer_1_out), .b(multiplexer_2_out), .eq(comparator_1_eq[0]), .lt(comparator_1_eq[1]));  // open: gt
  ROM #(.addrWidth(12), .dataWidth(16)) rom_1 (
    .addr({OPCODE_LATCH_q, counter_1_q}), .data({rom_1_data_2, rom_1_data, rom_1_data_3}));
  or or_5 (or_5_out, multiplexer_1_out[0], or_6_out, multiplexer_5_out[0]);
  Adder #(.width(16)) adder_2 (
    .a(IP_q), .b({{8{1'b0}}, rom_1_data_2, rom_1_data}), .out(adder_2_out));  // open: cin, cout
  Register #(.width(16)) ALU_OUT_LATCH (
    .D(controlled_buffer_1_out), .en(1'b1), .clk(shift_register_1_p5[0]));  // open: Q, clr
  Register FLAGS (.D(comparator_1_eq), .en(1'b1), .clk(shift_register_1_p5[0]));  // open: Q, clr
  Decoder #(.enable("false"), .select(4)) decoder_2 (
    .out0(decoder_2_out0), .out1(decoder_2_out1), .out3(decoder_2_out3), .out4(decoder_2_out4),
    .out5(decoder_2_out5), .sel(rom_1_data_3[3:0]));  // open: out2, out6, out7, out8, out9, out10, out11, out12, out13, out14, out15
  Decoder #(.select(4)) decoder_3 (
    .out0(decoder_3_out0), .out1(decoder_3_out1), .out2(decoder_3_out2), .out3(decoder_3_out3),
    .out4(decoder_3_out4), .out5(decoder_3_out5), .out6(decoder_3_out6), .out7(decoder_3_out7),
    .sel(rom_1_data_2), .en(decoder_2_out1));  // open: out8, out9, out10, out11, out12, out13, out14, out15
  assign controlled_buffer_4_out = not_2_out ? {16{1'b0}} : 16'bz;  // Controlled_Buffer controlled_buffer_5
  not not_2 (not_2_out, decoder_2_out1);
  Decoder #(.select(4)) decoder_4 (
    .out0(decoder_4_out0), .out1(decoder_4_out1), .out2(decoder_4_out2), .out3(decoder_4_out3),
    .out4(decoder_4_out4), .out5(decoder_4_out5), .sel(rom_1_data), .en(decoder_2_out1));  // open: out6, out7, out8, out9, out10, out11, out12, out13, out14, out15
  or or_6 (or_6_out, and_3_out, multiplexer_8_out[5]);
  Multiplexer #(.width(16)) multiplexer_4 (
    .in0(controlled_buffer_4_out), .in1(adder_3_out), .out(multiplexer_4_out), .sel(multiplexer_8_out[2]));
  and and_3 (and_3_out, multiplexer_8_out[2], ~rom_1_data[0]);  // AND_Gate
  Multiplexer #(.width(16)) multiplexer_5 (
    .in0({16{1'b0}}), .in1(shift_register_1_p5), .out(multiplexer_5_out), .sel(decoder_2_out1));
  Multiplexer #(.width(8)) multiplexer_6 (
    .in0(controlled_buffer_4_out[7:0]), .in1(controlled_buffer_4_out[15:8]), .out(multiplexer_6_out),
    .sel(decoder_3_out2));
  Clock clock_1 (.out(CLK));
  Register #(.width(16)) ADDR_LATCH (.D(multiplexer_4_out), .en(or_7_out), .clk(or_8_out), .Q(ADDRESS));  // open: clr
  or or_7 (or_7_out, decoder_3_out5, multiplexer_8_out[2]);
  or or_8 (or_8_out, multiplexer_8_out[3], multiplexer_5_out[0]);
  Multiplexer #(.width(16)) multiplexer_7 (
    .in0({16{1'b0}}), .in1(shift_register_1_p5), .out(multiplexer_7_out), .sel(decoder_2_out3));
  Register ACC_L (
    .D(controlled_buffer_4_out[7:0]), .en(or_9_out), .clk(multiplexer_5_out[0]), .Q(ACC_L_q));  // open: clr
  or or_9 (or_9_out, decoder_3_out0, decoder_3_out1);
  Register ACC_H (.D(multiplexer_6_out), .en(or_10_out), .clk(multiplexer_5_out[0]), .Q(ACC_H_q));  // open: clr
  or or_10 (or_10_out, decoder_3_out2, decoder_3_out1);
  assign controlled_buffer_4_out = decoder_4_out5 ? ADDRESS : 16'bz;  // Controlled_Buffer controlled_buffer_6
  Adder #(.width(16)) adder_3 (.a(ADDRESS), .b(16'h1), .out(adder_3_out));  // open: cin, cout
  Demultiplexer #(.width(8)) demultiplexer_1 (
    .out0(demultiplexer_1_out0), .out1(demultiplexer_1_out1), .in(ACC_H_q), .sel(decoder_4_out2));
  or or_11 (or_11_out, decoder_3_out3, and_4_out);
  and and_4 (and_4_out, multiplexer_8_out[1], multiplexer_8_out[3]);
  Multiplexer #(.width(16)) multiplexer_8 (
    .in0({16{1'b0}}), .in1(shift_register_1_p5), .out({multiplexer_8_out, MEM_O_EN}), .sel(decoder_2_out4));
  assign controlled_buffer_7_out = not_3_out ? ACC_L_q : 8'bz;  // Controlled_Buffer controlled_buffer_7
  not not_3 (not_3_out, decoder_4_out1);
  assign controlled_buffer_7_out = decoder_4_out1 ? demultiplexer_1_out0 : 8'bz;  // Controlled_Buffer controlled_buffer_8
  not not_4 (not_4_out, decoder_2_out4);
  or or_12 (or_12_out, decoder_3_out3, and_5_out);
  and and_5 (and_5_out, ~multiplexer_8_out[3], multiplexer_8_out[1]);  // AND_Gate
  xor xor_2 (xor_2_out, multiplexer_8_out[3], multiplexer_8_out[2]);
  assign controlled_buffer_4_out = or_13_out ? {demultiplexer_1_out1, controlled_buffer_7_out} : 16'bz;  // Controlled_Buffer controlled_buffer_9
  or or_13 (or_13_out, decoder_4_out0, decoder_4_out1, decoder_4_out2);
  assign controlled_buffer_10_out = not_4_out ? controlled_buffer_4_out : 16'bz;  // Controlled_Buffer controlled_buffer_10
  or or_14 (MEM_CLK, multiplexer_8_out[4], xor_3_out);
  xor xor_3 (xor_3_out, multiplexer_8_out[3], multiplexer_8_out[1]);
  or or_15 (or_15_out, multiplexer_5_out[0], multiplexer_8_out[5], xor_2_out);
  Register DATA_LATCH_L (
    .D(controlled_buffer_10_out[7:0]), .en(or_12_out), .clk(or_15_out), .Q(DATA_LATCH_L_q));  // open: clr
  Register DATA_LATCH_H (
    .D(controlled_buffer_10_out[15:8]), .en(or_11_out), .clk(or_15_out), .Q(DATA_LATCH_H_q), .clr(and_6_out));
  and and_6 (and_6_out, or_12_out, xor_2_out);
  Register #(.width(16)) SP ();  // open: D, en, clk, Q, clr
  Register #(.width(16)) BP ();  // open: D, en, clk, Q, clr
  Multiplexer #(.width(8)) multiplexer_9 (
    .in0(DATA_LATCH_L_q), .in1(DATA_LATCH_H_q), .out(multiplexer_9_out), .sel(or_11_out));
  Demultiplexer #(.tristate("true"), .width(8)) demultiplexer_2 (
    .out0(controlled_buffer_10_out[7:0]), .out1(controlled_buffer_10_out[15:8]),
    .in(controlled_buffer_11_out), .sel(or_11_out));
  assign controlled_buffer_11_out = multiplexer_8_out[1] ? DATA : 8'bz;  // Controlled_Buffer controlled_buffer_11
  assign DATA = multiplexer_7_out[0] ? multiplexer_9_out : 8'bz;  // Controlled_Buffer controlled_buffer_12
  assign controlled_buffer_4_out = decoder_4_out3 ? {DATA_LATCH_H_q, DATA_LATCH_L_q} : 16'bz;  // Controlled_Buffer controlled_buffer_13
  RAM #(.addrWidth(16), .databus("bidir")) ram_1 (
    .addr(ADDRESS), .oe(MEM_O_EN), .clk(MEM_CLK), .data(DATA));  // open: we

  // Other names for the same wires on the sheet: RST = in_1

  // Notes on the sheet:
  //   contents of rom_1 (hex, n*v repeats v):
  //   5401 4 110 6301
endmodule
